# Fritzing sketch 7seg_multi (saved by Fritzing 0.9.3b)
breadboards: 1

parts:
  LED1 = 7-SEGMENT-4DIGIT-YOUNGSUN [package=7-segment-4digit-youngsun-longpads]
  R1 = Resistor [tolerance=±5% resistance=330 package=THT]
  R2 = Resistor [tolerance=±5% resistance=330 package=THT]
  R3 = Resistor [tolerance=±5% resistance=330 package=THT]
  R4 = Resistor [tolerance=±5% resistance=330 package=THT]
  R5 = Resistor [tolerance=±5% resistance=330 package=THT]
  R6 = Resistor [tolerance=±5% resistance=330 package=THT]
  R7 = Resistor [tolerance=±5% resistance=330 package=THT]
  R1-R8 = Resistor [tolerance=±5% resistance=330 package=THT]
  Q1 = NPN-Transistor [package="TO92 [THT]"]
  Q2 = NPN-Transistor [package="TO92 [THT]"]
  Q3 = NPN-Transistor [package="TO92 [THT]"]
  Q1-Q4 = NPN-Transistor [part_number="2N 3904" package="TO92 [THT]"]
  R9-R12 = Resistor [tolerance=±5% resistance=33k package=THT]
  R10 = Resistor [tolerance=±5% resistance=33k package=THT]
  R11 = Resistor [tolerance=±5% resistance=33k package=THT]
  R12 = Resistor [tolerance=±5% resistance=33k package=THT]
  Raspberry_Pi_1 = Raspberry Pi 2

nets:
  N1: LED1.DIG1, Q1.C
  N2: LED1.DIG2, Q2.C
  N3: LED1.D, R4.Pin_1
  N4: LED1.E, R7.Pin_1
  N5: LED1.DIG3, Q3.C
  N6: LED1.DP, R1-R8.Pin_1
  N7: LED1.DIG4, Q1-Q4.C
  N8: LED1.F, R5.Pin_0
  N9: LED1.C, R3.Pin_1
  N10: LED1.A, R1.Pin_1
  N11: LED1.G, R6.Pin_0
  N12: LED1.B, R2.Pin_1
  N13: R1.Pin_0, Raspberry_Pi_1.GIPO22
  N14: R2.Pin_0, Raspberry_Pi_1.GIPO23
  N15: R3.Pin_0, Raspberry_Pi_1.GIPO24
  N16: R4.Pin_0, Raspberry_Pi_1.GIPO25
  N17: R5.Pin_1, Raspberry_Pi_1.GIPO20
  N18: R6.Pin_1, Raspberry_Pi_1.GIPO16
  N19: R7.Pin_0, Raspberry_Pi_1.GIPO21
  N20: R1-R8.Pin_0, Raspberry_Pi_1.GIPO12
  N21: Q1.E, Q2.E, Q3.E, Q1-Q4.E, Raspberry_Pi_1.GND
  N22: Q1.B, R9-R12.Pin_0
  N23: Q2.B, R10.Pin_0
  N24: Q3.B, R11.Pin_0
  N25: Q1-Q4.B, R12.Pin_0
  N26: R9-R12.Pin_1, Raspberry_Pi_1.GIPO26
  N27: R10.Pin_1, Raspberry_Pi_1.GIPO19
  N28: R11.Pin_1, Raspberry_Pi_1.GIPO13
  N29: R12.Pin_1, Raspberry_Pi_1.GIPO6
