# Fritzing sketch button_robot (saved by Fritzing 0.9.2b)
breadboards: 1

parts:
  Raspberry_Pi1 = Raspberry Pi 2
  M2 = DC Motor
  M3 = DC Motor
  IC1 = H-Bridge [package=THT]
  S1 = Pushbutton [package="[THT]"]
  S2 = Pushbutton [package="[THT]"]
  S3 = Pushbutton [package="[THT]"]
  S4 = Pushbutton [package="[THT]"]

nets:
  N1: Raspberry_Pi1.GPIO4, IC1.4A
  N2: Raspberry_Pi1.GPIO17, IC1.1A
  N3: Raspberry_Pi1.GPIO26, S1.Pin_3, S1.Pin_4
  GND: Raspberry_Pi1.GND, IC1.GND1, IC1.GND2, IC1.GND3, IC1.GND4, S1.Pin_1, S1.Pin_2, S2.Pin_1, S2.Pin_2, S3.Pin_1, S3.Pin_2, S4.Pin_1, S4.Pin_2
  N4: Raspberry_Pi1.GPIO21, S4.Pin_3, S4.Pin_4
  N5: Raspberry_Pi1.GPIO20, S3.Pin_3, S3.Pin_4
  N6: Raspberry_Pi1.GPIO16, S2.Pin_3, S2.Pin_4
  N7: Raspberry_Pi1.GPIO18, IC1.2A
  N8: Raspberry_Pi1.GPIO14, IC1.3A
  N9: Raspberry_Pi1.5V, IC1.1_2EN, IC1.VCC2, IC1.3_4EN, IC1.VCC1
  N10: M2.pin_1, IC1.4Y
  N11: M2.pin_2, IC1.3Y
  N12: M3.pin_1, IC1.2Y
  N13: M3.pin_2, IC1.1Y
