# Fritzing sketch color_picker (saved by Fritzing 0.9.3b)
breadboards: 1

parts:
  Raspberry_Pi_1 = Raspberry Pi 3 [part_number=RPI-3-V1.2]
  RE1 = Rotary Encoder [package=THT]
  R1 = Resistor [tolerance=±5% resistance=330 package=THT]
  R2 = Resistor [tolerance=±5% resistance=330 package=THT]
  R3 = Resistor [tolerance=±5% resistance=330 package=THT]
  LED1 = RGB LED - (4 legs) [package="5 mm [THT]"]
  S1 = Pushbutton [package="[THT]"]

nets:
  3V3: Raspberry_Pi_1.3v3, Raspberry_Pi_1.3V3, LED1.common_anode, S1.Pin_1, S1.Pin_2
  N1: Raspberry_Pi_1.GIPO22, R1.Pin_0
  N2: Raspberry_Pi_1.GND, RE1.EncoderPinC
  N3: Raspberry_Pi_1.GIPO21, S1.Pin_3, S1.Pin_4
  N4: Raspberry_Pi_1.GIPO20, RE1.EncoderPinB
  N5: Raspberry_Pi_1.GIPO16, RE1.EncoderPinA
  N6: Raspberry_Pi_1.GIPO24, R3.Pin_0
  N7: Raspberry_Pi_1.GIPO23, R2.Pin_0
  N8: R1.Pin_1, LED1.red_cathode
  N9: R2.Pin_1, LED1.green_cathode
  N10: R3.Pin_1, LED1.blue_cathode
