# Fritzing sketch led_button (saved by Fritzing 0.9.2b)
breadboards: 1

parts:
  LED1 = LED - 5mm [color="Red (633nm)" package="5 mm [THT]"]
  Raspberry_Pi1 = Raspberry Pi 2
  S1 = Pushbutton [package="[THT]"]
  R1 = Resistor [tolerance=±5% resistance=330 package=THT]

nets:
  N1: LED1.cathode, Raspberry_Pi1.GND, S1.Pin_1, S1.Pin_2
  N2: LED1.anode, R1.Pin_0
  N3: Raspberry_Pi1.GPIO2, S1.Pin_3, S1.Pin_4
  N4: Raspberry_Pi1.GPIO17, R1.Pin_1
