# Fritzing sketch led_char_display (saved by Fritzing 0.9.3b)
breadboards: 1

parts:
  Raspberry_Pi_1 = Raspberry Pi 2
  7_Segment1 = 7 Segment Display
  R1 = Resistor [tolerance=±5% resistance=330 package=THT]
  R2 = Resistor [tolerance=±5% resistance=330 package=THT]
  R3 = Resistor [tolerance=±5% resistance=330 package=THT]
  R4 = Resistor [tolerance=±5% resistance=330 package=THT]
  R5 = Resistor [tolerance=±5% resistance=330 package=THT]
  R6 = Resistor [tolerance=±5% resistance=330 package=THT]
  R7 = Resistor [tolerance=±5% resistance=330 package=THT]
  R8 = Resistor [tolerance=±5% resistance=330 package=THT]

nets:
  N1: Raspberry_Pi_1.GIPO22, R1.Pin_0
  N2: Raspberry_Pi_1.GND, 7_Segment1.common_cathode
  N3: Raspberry_Pi_1.GIPO21, R5.Pin_1
  N4: Raspberry_Pi_1.GIPO20, R6.Pin_1
  N5: Raspberry_Pi_1.GIPO16, R7.Pin_1
  N6: Raspberry_Pi_1.GIPO12, R8.Pin_1
  N7: Raspberry_Pi_1.GIPO25, R4.Pin_0
  N8: Raspberry_Pi_1.GIPO24, R3.Pin_0
  N9: Raspberry_Pi_1.GIPO23, R2.Pin_0
  N10: 7_Segment1.Segment_A#1, R8.Pin_0
  N11: 7_Segment1.Segment_F, R7.Pin_0
  N12: 7_Segment1.Segment_E, R6.Pin_0
  N13: 7_Segment1.Segment_D, R5.Pin_0
  N14: 7_Segment1.Segment_DP, R4.Pin_1
  N15: 7_Segment1.Segment_C, R3.Pin_1
  N16: 7_Segment1.Segment_B, R2.Pin_1
  N17: 7_Segment1.Segment_A#10, R1.Pin_1
