# Fritzing sketch ledboard (saved by Fritzing 0.9.2b)
breadboards: 1

parts:
  Raspberry_Pi1 = Raspberry Pi 2
  LED4 = LED - 5mm [color="Green (555nm)" package="5 mm [THT]"]
  LED5 = LED - 5mm [color="Green (570nm)" package="5 mm [THT]"]
  LED6 = LED - 5mm [color="Yellow (592nm)" package="5 mm [THT]"]
  LED7 = LED - 5mm [color="Orange (612nm)" package="5 mm [THT]"]
  LED8 = LED - 5mm [color="Red (633nm)" package="5 mm [THT]"]
  R1 = Resistor [tolerance=±5% resistance=330 package=THT]
  R2 = Resistor [tolerance=±5% resistance=330 package=THT]
  R3 = Resistor [tolerance=±5% resistance=330 package=THT]
  R4 = Resistor [tolerance=±5% resistance=330 package=THT]
  R5 = Resistor [tolerance=±5% resistance=330 package=THT]

nets:
  N1: Raspberry_Pi1.GPIO5, LED8.anode
  N2: Raspberry_Pi1.GPIO6, LED7.anode
  N3: Raspberry_Pi1.GPIO13, LED6.anode
  N4: Raspberry_Pi1.GPIO19, LED5.anode
  N5: Raspberry_Pi1.GPIO26, LED4.anode
  N6: Raspberry_Pi1.GND, R1.Pin_0, R2.Pin_0, R3.Pin_0, R4.Pin_0, R5.Pin_0
  N7: LED4.cathode, R5.Pin_1
  N8: LED5.cathode, R4.Pin_1
  N9: LED6.cathode, R3.Pin_1
  N10: LED7.cathode, R2.Pin_1
  N11: LED8.cathode, R1.Pin_1
