# Fritzing sketch motion_robot (saved by Fritzing 0.9.2b)
breadboards: 1

parts:
  Raspberry_Pi1 = Raspberry Pi 2
  M2 = DC Motor
  M3 = DC Motor
  IC1 = H-Bridge [package=THT]
  Part1 = HC-SR501 Body Sensor Module

nets:
  N1: Raspberry_Pi1.GPIO4, IC1.4A
  N2: Raspberry_Pi1.GPIO17, IC1.1A
  N3: Raspberry_Pi1.GPIO5, Part1.OUT
  GND: Raspberry_Pi1.GND, IC1.GND1, IC1.GND2, IC1.GND3, IC1.GND4, Part1.GND
  N4: Raspberry_Pi1.GPIO18, IC1.2A
  N5: Raspberry_Pi1.GPIO14, IC1.3A
  5V: Raspberry_Pi1.5V, IC1.1_2EN, IC1.VCC2, IC1.3_4EN, IC1.VCC1, Part1.VCC
  N6: M2.pin_1, IC1.4Y
  N7: M2.pin_2, IC1.3Y
  N8: M3.pin_1, IC1.2Y
  N9: M3.pin_2, IC1.1Y

custom parts:
  HC-SR501 Body Sensor Module: Pyroelectric Infrared PIR Motion Sensor Detector Module
