# Fritzing sketch motion_sensor (saved by Fritzing 0.9.2b)
breadboards: 1

parts:
  Raspberry_Pi1 = Raspberry Pi 2
  LED2 = LED - 5mm [color="Red (633nm)" package="5 mm [THT]"]
  R2 = Resistor [tolerance=±5% resistance=330 package=THT]
  Part1 = HC-SR501 Body Sensor Module

nets:
  N1: Raspberry_Pi1.GPIO4, Part1.OUT
  GND: Raspberry_Pi1.GND, R2.Pin_0, Part1.GND
  N2: Raspberry_Pi1.GPIO16, LED2.anode
  5V: Raspberry_Pi1.5V, Part1.VCC
  N3: LED2.cathode, R2.Pin_1

custom parts:
  HC-SR501 Body Sensor Module: Pyroelectric Infrared PIR Motion Sensor Detector Module
