# Fritzing sketch motor (saved by Fritzing 0.9.2b)
breadboards: 1

parts:
  Raspberry_Pi1 = Raspberry Pi 2
  IC1 = H-Bridge [package=THT]
  M2 = DC Motor

nets:
  N1: Raspberry_Pi1.GPIO4, IC1.3A
  N2: Raspberry_Pi1.GPIO14, IC1.4A
  GND: Raspberry_Pi1.GND, IC1.GND1, IC1.GND2, IC1.GND3, IC1.GND4
  N3: Raspberry_Pi1.5V, IC1.1_2EN, IC1.VCC2, IC1.3_4EN, IC1.VCC1
  N4: IC1.3Y, M2.pin_2
  N5: IC1.4Y, M2.pin_1
