# Fritzing sketch music_box (saved by Fritzing 0.9.2b)
breadboards: 1

parts:
  Raspberry_Pi1 = Raspberry Pi 2
  S1 = Pushbutton [package="[THT]"]
  S2 = Pushbutton [package="[THT]"]

nets:
  N1: Raspberry_Pi1.GPIO2, S1.Pin_1, S1.Pin_2
  N2: Raspberry_Pi1.GPIO3, S2.Pin_1, S2.Pin_2
  N3: Raspberry_Pi1.GND, S1.Pin_3, S1.Pin_4, S2.Pin_3, S2.Pin_4
