# Fritzing sketch potentiometer (saved by Fritzing 0.9.2b)
breadboards: 1

parts:
  R1 = Rotary Potentiometer (Small) [maximum_resistance=100kΩ package=THT]
  IC1 = IC, DIP package, 16 pins [chip_label=MCP3008]
  Raspberry_Pi1 = Raspberry Pi 2
  R2 = Resistor [tolerance=±5% resistance=330 package=THT]
  R3 = Resistor [tolerance=±5% resistance=330 package=THT]
  R4 = Resistor [tolerance=±5% resistance=330 package=THT]
  R5 = Resistor [tolerance=±5% resistance=330 package=THT]
  R6 = Resistor [tolerance=±5% resistance=330 package=THT]
  LED1 = LED - 5mm [color="Red (633nm)" package="5 mm [THT]"]
  LED2 = LED - 5mm [color="Orange (612nm)" package="5 mm [THT]"]
  LED3 = LED - 5mm [color="Yellow (585nm)" package="5 mm [THT]"]
  LED4 = LED - 5mm [color="Green (570nm)" package="5 mm [THT]"]
  LED5 = LED - 5mm [color="Green (555nm)" package="5 mm [THT]"]

nets:
  N1: R1.leg1, IC1.pin9, IC1.pin14, Raspberry_Pi1.GND, LED1.cathode, LED2.cathode, LED3.cathode, LED4.cathode, LED5.cathode
  N2: R1.wiper, IC1.pin1
  N3: R1.leg2, IC1.pin15, IC1.pin16, Raspberry_Pi1.3v3
  N4: IC1.pin10, Raspberry_Pi1.GPIO8
  N5: IC1.pin11, Raspberry_Pi1.GPIO10
  N6: IC1.pin12, Raspberry_Pi1.GPIO9
  N7: IC1.pin13, Raspberry_Pi1.GPIO11
  N8: Raspberry_Pi1.GPIO5, R2.Pin_1
  N9: Raspberry_Pi1.GPIO6, R3.Pin_1
  N10: Raspberry_Pi1.GPIO13, R4.Pin_1
  N11: Raspberry_Pi1.GPIO19, R5.Pin_1
  N12: Raspberry_Pi1.GPIO26, R6.Pin_1
  N13: R2.Pin_0, LED5.anode
  N14: R3.Pin_0, LED4.anode
  N15: R4.Pin_0, LED3.anode
  N16: R5.Pin_0, LED2.anode
  N17: R6.Pin_0, LED1.anode
