# Fritzing sketch rgb_led (saved by Fritzing 0.9.2b)
breadboards: 1

parts:
  Raspberry_Pi1 = Raspberry Pi 2
  LED1 = RGB LED (com. cathode, rgb) [package="5 mm [THT]"]
  R1 = Resistor [tolerance=±5% resistance=330 package=THT]
  R2 = Resistor [tolerance=±5% resistance=330 package=THT]
  R3 = Resistor [tolerance=±5% resistance=330 package=THT]  # not connected

nets:
  N1: Raspberry_Pi1.GPIO9, R1.Pin_0
  N2: Raspberry_Pi1.GPIO11, R2.Pin_0
  N3: Raspberry_Pi1.GND, LED1.common_cathode
  N4: LED1.red_anode, R1.Pin_1
  N5: LED1.blue_anode, R2.Pin_1
