# Fritzing sketch rgbled_pot (saved by Fritzing 0.9.2b)
breadboards: 1

parts:
  IC1 = IC, DIP package, 16 pins [chip_label=MCP3008]
  Raspberry_Pi1 = Raspberry Pi 2
  R3 = Resistor [tolerance=±5% resistance=330 package=THT]
  R4 = Resistor [tolerance=±5% resistance=330 package=THT]
  R6 = Resistor [tolerance=±5% resistance=330 package=THT]
  LED1 = RGB LED (com. cathode, rgb) [package="5 mm [THT]"]
  R7 = Trimmer Potentiometer [maximum_resistance=10kΩ package=THT]
  R8 = Trimmer Potentiometer [maximum_resistance=10kΩ package=THT]
  R9 = Trimmer Potentiometer [maximum_resistance=10kΩ package=THT]

nets (from the schematic view):
  N1: IC1.pin1, R9.wiper
  N2: IC1.pin2, R8.wiper
  N3: IC1.pin3, R7.wiper
  N4: IC1.pin9, IC1.pin14, Raspberry_Pi1.GND, LED1.common_cathode, R7.leg2, R8.leg2, R9.leg2
  N5: IC1.pin10, Raspberry_Pi1.GPIO8
  N6: IC1.pin11, Raspberry_Pi1.GPIO10
  N7: IC1.pin12, Raspberry_Pi1.GPIO9
  N8: IC1.pin13, Raspberry_Pi1.GPIO11
  N9: IC1.pin15, IC1.pin16, Raspberry_Pi1.3v3, R7.leg1, R8.leg1, R9.leg1
  N10: Raspberry_Pi1.GPIO2, R6.Pin_1
  N11: Raspberry_Pi1.GPIO3, R3.Pin_1
  N12: Raspberry_Pi1.GPIO4, R4.Pin_1
  N13: R3.Pin_0, LED1.blue_anode
  N14: R4.Pin_0, LED1.green_anode
  N15: R6.Pin_0, LED1.red_anode
